// Logisim project Condition.circ as structural Verilog: 2 circuits, main circuit main
module main (
  input  lt,
  input  eq,
  input  gt,
  input  [15:0] X
);

  wire less_than_zero_1_out_2;

  Less_than_zero less_than_zero_1 (.in_1(X), .out_2(less_than_zero_1_out_2));
  // NOT_Gate not_1 has open pins: in=less_than_zero_1_out_2, out=open
endmodule

module Less_than_zero (
  input  [15:0] in_1,
  output out_2
);


  assign out_2 = in_1[15];
endmodule
